# Fritzing sketch Fall Detection Schematics (saved by Fritzing 0.9.4)

parts:
  U1 = NodeMCU V1.0
  Part1 = InvenSense MPU6050

nets:
  N1: U1.D1, Part1.SCL
  N2: U1.D2, Part1.SDA
  3V3: U1.3V3, Part1.VCC
  GND: U1.GND, Part1.GND

custom parts:
  NodeMCU V1.0: ESP8266 based NodeMCU
