# Fritzing sketch Shravan Schematics (saved by Fritzing 0.8.3b)
breadboards: 1

parts:
  Part1 = SRF05 Ultrasonic Rangefinder
  Raspberry_Pi_1 = Raspberry Pi 4 [part_number=RPI-4-b]
  R1 = Resistor [tolerance=±5% resistance=330 package=THT]
  R2 = Resistor [tolerance=±5% resistance=47 package=THT]
  J1 = Piezo Speaker
  S1 = Pushbutton [package="[THT]"]
  S2 = Pushbutton [package="[THT]"]
  U1 = Vibration Motor- ROB-08449 [package=vibe-motor-10mm]

nets:
  VCC: Part1.VCC, Raspberry_Pi_1.5V
  N1: Part1.Trig, Raspberry_Pi_1.GPIO4
  N2: Part1.Echo, R1.Pin_0
  GND: Part1.GND, Raspberry_Pi_1.GND, R2.Pin_1, J1.pin1, S1.Pin_3, S1.Pin_4, S2.Pin_3, S2.Pin_4, U1.+
  N3: Raspberry_Pi_1.GPIO2, S1.Pin_1, S1.Pin_2
  N4: Raspberry_Pi_1.GPIO17, R1.Pin_1, R2.Pin_0
  N5: Raspberry_Pi_1.GPIO5, J1.pin2
  N6: Raspberry_Pi_1.GPIO24, U1.-
  N7: Raspberry_Pi_1.GPIO18, S2.Pin_1, S2.Pin_2

custom parts:
  Raspberry Pi 4: The RPi4, a faster version of the awesome Raspberry Pi 2 B ARM Board with 40 pin gpio. Ready for special Raspberry Pi B+ and RPi2 Hat (Hardware attached (on) top)
